# Fritzing sketch sensor (saved by Fritzing 0.9.2b)
breadboards: 1

parts:
  K1 = Relay [part_number=FRS1B-S package=THT]
  R3 = Resistor [tolerance=±5% resistance=300k package=THT]
  Q1 = NPN-Transistor [package="TO92 [THT]"]
  D1 = Rectifier Diode [part_number=1N4001 package="300 mil [THT]"]
  IC1 = DIP - 8 pins [part_number=LM741 package="DIP (Dual Inline) [THT]"]
  C1 = Ceramic Capacitor [capacitance=1µF package="100 mil [THT, multilayer]"]
  R2 = Resistor [tolerance=±5% resistance=100k package=THT]
  R1 = Resistor [tolerance=±5% resistance=100k package=THT]
  R4 = Resistor [tolerance=±5% resistance=1M package=THT]
  S1 = Pushbutton [package=THT]
  VCC1 = Battery block 9V

nets:
  N1: K1.A, K1.C1
  N2: K1.COIL1, Q1.C, D1.cathode
  N3: R3.Pin_0, IC1.pin6
  N4: R3.Pin_1, Q1.B
  N5: Q1.E, IC1.pin4, R1.Pin_0, S1.leg1, VCC1.-
  N6: D1.anode, IC1.pin7, C1.1, R2.Pin_0, S1.leg0
  N7: IC1.pin2, C1.0, R4.Pin_1
  N8: IC1.pin3, R2.Pin_1, R1.Pin_1

custom parts:
  DIP - 8 pins: A DIP stand-in part for whatever IC you want. With 8 pins on a 300 mil dual inline package (DIP) footprint.
